# Fritzing sketch OpenSplashPad (saved by Fritzing 0.9.0b)
circuit board: 9.92656cm x 8.29363cm
breadboards: 1

parts:
  XTAL1 = Crystal [frequency="16 Mhz" package=THT]
  Relay8 = Relay T73 [part_number=SRD-5VDC-SL-C]
  Relay7 = Relay T73 [part_number=SRD-5VDC-SL-C]
  J6 = Screw terminal - 2 pins [package=THT]
  Relay1 = Relay T73
  Relay2 = Relay T73 [part_number=SRD-5VDC-SL-C]
  Relay6 = Relay T73
  Relay5 = Relay T73
  Relay3 = Relay T73
  Relay4 = Relay T73 [part_number=SRD-5VDC-SL-C]
  DA1 = ULN2803A [package=THT]
  Part8 = Relay T73
  J10 = Screw terminal - 2 pins [package=THT]
  J7 = female pin header, 6 pins [form="♀ (female)"]
  R11 = Resistor [tolerance=±5% resistance=1k package=THT]
  Q1 = NPN-Transistor [package="TO92 [THT]"]
  R11_2 = Resistor [tolerance=±5% resistance=1k package=THT]
  R12 = Resistor [tolerance=±5% resistance=10k package=THT]
  J13 = Screw terminal - 2 pins [package=THT]
  J14 = female pin header, 6 pins [form="♀ (female)"]
  C2 = Ceramic Capacitor [capacitance=100nF part_number=SR151A220JARTR1 voltage=50V package="100 mil [THT, multilayer]"]
  C3 = Ceramic Capacitor [capacitance=0.1µF part_number=C104 voltage=50V package="100 mil [THT, multilayer]"]
  C1 = Ceramic Capacitor [capacitance=10pF voltage=50V part_number=SR151A220JARTR1 package="100 mil [THT, multilayer]"]
  S1 = Pushbutton [package="[THT]"]
  PWR = LED - 3mm [color="Red (633nm)" package="3 mm [THT]"]
  RUN = LED - 3mm [color="Red (633nm)" package="3 mm [THT]"]
  R10 = Resistor [tolerance=±5% resistance=10k package=THT]
  U1 = atmega168 [package=dip]
  J12 = screw terminal, 2 pins
  C4 = Ceramic Capacitor [capacitance=0.1µF part_number=C104 voltage=50V package="100 mil [THT, multilayer]"]
  C5 = Electrolytic Capacitor [capacitance=1µF voltage=16V package="100 mil [THT, electrolytic]"]
  D8 = Rectifier Diode [package="Melf DO-213 AA [SMD]"]
  D7 = Rectifier Diode [package="Melf DO-213 AA [SMD]"]
  D6 = Rectifier Diode [package="Melf DO-213 AA [SMD]"]
  D5 = Rectifier Diode [package="Melf DO-213 AA [SMD]"]
  D4 = Rectifier Diode [package="Melf DO-213 AA [SMD]"]
  D3 = Rectifier Diode [package="Melf DO-213 AA [SMD]"]
  D2 = Rectifier Diode [package="Melf DO-213 AA [SMD]"]
  D1 = Rectifier Diode [package="Melf DO-213 AA [SMD]"]
  C6 = Electrolytic Capacitor [capacitance=10µF package="100 mil [THT, electrolytic]"]
  C7 = Electrolytic Capacitor [capacitance=10µF package="100 mil [THT, electrolytic]"]
  J9 = screw terminal, 16 pins
  R3 = Resistor [tolerance=±5% resistance=10k package="0603 [SMD]"]
  LED3 = smd LED [color="Red (633nm)" package="0603 [SMD]"]
  R5 = Resistor [tolerance=±5% resistance=1k package="0603 [SMD]"]
  R4 = Resistor [tolerance=±5% resistance=10k package="0603 [SMD]"]
  LED4 = smd LED [color="Red (633nm)" package="0603 [SMD]"]
  LED2 = smd LED [color="Red (633nm)" package="0603 [SMD]"]
  R2 = Resistor [tolerance=±5% resistance=10k package="0603 [SMD]"]
  R1 = Resistor [tolerance=±5% resistance=10k package="0603 [SMD]"]
  LED1 = smd LED [color="Red (633nm)" package="0603 [SMD]"]
  LED5 = smd LED [color="Red (633nm)" package="0603 [SMD]"]
  LED6 = smd LED [color="Red (633nm)" package="0603 [SMD]"]
  LED7 = smd LED [color="Red (633nm)" package="0603 [SMD]"]
  LED8 = smd LED [color="Red (633nm)" package="0603 [SMD]"]
  R6 = Resistor [tolerance=±5% resistance=1k package="0603 [SMD]"]
  R7 = Resistor [tolerance=±5% resistance=1k package="0603 [SMD]"]
  R8 = Resistor [tolerance=±5% resistance=1k package="0603 [SMD]"]
  R9 = Resistor [tolerance=±5% resistance=2.2k package="0603 [SMD]"]
  LED9 = smd LED [color="Red (633nm)" package="0603 [SMD]"]
  D9 = Rectifier Diode [package="Melf DO-213 AA [SMD]"]
  S2 = Pushbutton [package="[THT]"]

nets:
  N1: XTAL1.pin_0, C1.0, U1.XLAT2
  N2: XTAL1.pin_1, C2.0, U1.XLAT1
  N3: Relay8.C1, Relay7.C1, J6.pin2, Relay1.C2, Relay2.C2, Relay6.C1, Relay5.C1, Relay3.C2, Relay4.C2, DA1.COM_-_Common, Part8.C1, J7.pin3, R12.Pin_1, PWR.anode, U1.VCC, U1.AVCC, U1.AREF, C4.0, C5.+, D8.cathode, D7.cathode, D6.cathode, D5.cathode, D4.cathode, D3.cathode, D2.cathode, D1.cathode, C6.+, C7.+, LED3.anode, LED4.anode, LED2.anode, LED1.anode, LED5.anode, LED6.anode, LED7.anode, LED8.anode, LED9.anode, D9.cathode
  N4: Relay8.C2, DA1.Out_1, D8.anode, R8.Pin_0
  N5: Relay8.COM, Relay7.COM, Relay1.COM, Relay2.COM, Relay6.COM, Relay5.COM, Relay3.COM, Relay4.COM, J13.pin1
  N6: Relay8.NO, J9.pin15
  N7: Relay7.C2, DA1.Out_2, D7.anode, R7.Pin_0
  N8: Relay7.NO, J9.pin13
  GND: J6.pin1, DA1.0V, J7.pin1, R11.Pin_0, Q1.E, C2.1, C1.1, S1.Pin_3, S1.Pin_4, R10.Pin_0, U1.GND, J12.pin1, C4.1, C5.-, C6.-, C7.-, S2.Pin_1, S2.Pin_2
  N9: Relay1.C1, DA1.Out_8, D1.anode, R1.Pin_1
  N10: Relay1.NO, J9.pin1
  N11: Relay2.C1, DA1.Out_7, D2.anode, R2.Pin_1
  N12: Relay2.NO, J9.pin3
  N13: Relay6.C2, DA1.Out_3, D6.anode, R6.Pin_0
  N14: Relay6.NO, J9.pin11
  N15: Relay5.C2, DA1.Out_4, D5.anode, R5.Pin_0
  N16: Relay5.NO, J9.pin9
  N17: Relay3.C1, DA1.Out_6, D3.anode, R3.Pin_1
  N18: Relay3.NO, J9.pin5
  N19: Relay4.C1, DA1.Out_5, D4.anode, R4.Pin_1
  N20: Relay4.NO, J9.pin7
  N21: DA1.In_1, U1.D12
  N22: DA1.In_2, U1.D11_(PWM)
  N23: DA1.In_3, U1.D10_(PWM)
  N24: DA1.In_4, U1.D9_(PWM)
  N25: DA1.In_5, U1.D8
  N26: DA1.In_6, U1.D7
  N27: DA1.In_7, U1.D6_(PWM)
  N28: DA1.In_8, U1.D5_(PWM)
  N29: Part8.C2, Q1.C, R9.Pin_1, D9.anode
  N30: Part8.COM, J10.pin2
  N31: Part8.NO, J10.pin1
  N32: J7.pin4, U1.D0_(RX)
  N33: J7.pin5, U1.D1_(TX)
  N34: J7.pin6, C3.1
  N35: R11.Pin_1, RUN.cathode
  N36: Q1.B, R11_2.Pin_1
  N37: R11_2.Pin_0, U1.D2
  N38: R12.Pin_0, C3.0, S1.Pin_1, S1.Pin_2, U1.RESET
  N39: J13.pin2, J9.pin2, J9.pin4, J9.pin6, J9.pin8, J9.pin10, J9.pin12, J9.pin14, J9.pin16
  N40: J14.pin1, U1.A5
  N41: J14.pin2, U1.A4
  N42: J14.pin3, U1.A3
  N43: J14.pin4, U1.A2
  N44: J14.pin5, U1.A1
  N45: J14.pin6, U1.A0
  N46: PWR.cathode, R10.Pin_1
  N47: RUN.anode, U1.D13
  N48: U1.D4, J12.pin2, S2.Pin_3, S2.Pin_4
  N49: R3.Pin_0, LED3.cathode
  N50: R5.Pin_1, LED5.cathode
  N51: R4.Pin_0, LED4.cathode
  N52: LED2.cathode, R2.Pin_0
  N53: R1.Pin_0, LED1.cathode
  N54: LED6.cathode, R6.Pin_1
  N55: LED7.cathode, R7.Pin_1
  N56: LED8.cathode, R8.Pin_1
  N57: R9.Pin_0, LED9.cathode

notes:
  +
  -
  5V
  A0-A5
  COM
  1(D5)
  2(D6)
  3(D7)
  4(D8)
  5(D9)
  6(D10)
  7(D11)
  8(D12)
  Relay Pwr
  Relay Contacts
  Input(D4)
  Designed by Chad Davis 2015
  cradleofintrigue.com
  Reset
  Splash Pad Controller rev2
  Motor(D2)
  Man Start

custom parts:
  Relay T73: An T73 Mini PCB Relay
